// Logisim project canonical_suite.circ as structural Verilog: 4 circuits, main circuit main
module main (
  input  A0,
  input  A1,
  input  E,
  output Y0,
  output Y1,
  output Y2,
  output Y3
);

  wire not_1_out, not_2_out;

  not not_1 (not_1_out, A0);
  not not_2 (not_2_out, A1);
  and u_Y0 (Y0, not_2_out, not_1_out, E);
  and u_Y1 (Y1, not_2_out, A0, E);
  and u_Y2 (Y2, A1, not_1_out, E);
  and u_Y3 (Y3, A1, A0, E);
endmodule

module \Классический_8_в_3  (
  input  X0,
  input  X1,
  input  X2,
  input  X3,
  input  X4,
  input  X5,
  input  X6,
  input  X7,
  output Y0__1,
  output Y1__2,
  output Y2__4
);

  or OR_Y0 (Y0__1, X1, X1, X5, X2);
  or OR_Y1 (Y1__2, X2, X1, X5, X2);
  or OR_Y2 (Y2__4, X2, X5, X5, X2);

  assign X3 = X1;
  assign X4 = X2;
  assign X6 = X5;
  assign X7 = X2;
endmodule

module \Мультиплексор_4_в_1  (
  input  D0,
  input  D1,
  input  D2,
  input  D3,
  input  A0,
  input  A1,
  input  E,
  output Y
);

  wire AND_0_out, AND_1_out, AND_2_out, AND_3_out, not_1_out, not_2_out;

  not not_1 (not_1_out, A0);
  not not_2 (not_2_out, A1);
  and AND_0 (AND_0_out, D0, not_2_out, not_1_out, E);
  and AND_1 (AND_1_out, D1, not_2_out, A0, E);
  and AND_2 (AND_2_out, D2, A1, not_1_out, E);
  and AND_3 (AND_3_out, D3, A1, A0, E);
  or OR_OUT (Y, AND_0_out, AND_1_out, AND_2_out, AND_3_out);
endmodule

module \Демультиплексор_1_в_4  (
  input  DI,
  input  E,
  input  A0,
  input  A1,
  output Y0,
  output Y1,
  output Y2,
  output Y3
);

  wire not_1_out, not_2_out;

  not not_1 (not_1_out, A0);
  not not_2 (not_2_out, A1);
  and AND_0 (Y0, DI, not_2_out, not_1_out, E);
  and AND_1 (Y1, DI, not_2_out, A0, E);
  and AND_2 (Y2, DI, A1, not_1_out, E);
  and AND_3 (Y3, DI, A1, A0, E);
endmodule
